// Digital circuit main.dig as structural Verilog
module main (
  input  clk
);

  wire A_WR_DB, ADDR_RS0_A, ADDR_RS0_B, ADDR_RS0_C, ADDR_RS0_D, ADDR_RS1_A, ADDR_RS1_B, ADDR_RS1_C,
       ADDR_RS1_D, ALU_A_IN_A, ALU_A_IN_B, ALU_B_IN_A, ALU_B_IN_B, ALU_C_IN_A, ALU_C_IN_B, ALU_D_IN_A,
       ALU_D_IN_B, B_WR_DB, C_WR_DB, D_WR_DB, imm16, IR0_RD, IR1_RD, IR2_RD, nand_1_out, ooo, or_1_out,
       PC_2_ovf, PC_H_RD, PC_INC, PC_L_RD, PC_ovf, REG_A_RD, REG_B_RD, REG_C_RD, REG_D_RD, SP_DEC, SP_H_RD,
       SP_H_WR_DB, SP_INC, SP_L_RD, SP_L_WR_DB;
  wire [1:0] ll, microcode_1_ab_wr_dev;
  wire [2:0] DB_WR_DEV, REG_RD, rs0, rs1, vvv;
  wire [3:0] alu_1_p5, alu_1_p6;
  wire [7:0] A_q, ACC_q, alu_1_p4, B_q, C_q, D_q, driver_3_out, driver_19_out, imm8,
       instruction_decoder_1_p1, instruction_decoder_1_p6, instruction_decoder_1_p8, IR0_D, PC_2_hi, PC_2_lo,
       PC_hi, PC_lo;
  wire [15:0] driver_1_out, driver_8_out;

  // Probe on REG_RD
  // Probe on DB_WR_DEV
  microcode microcode_1 (
    .d0(IR0_D), .c(clk), .PC_INC(PC_INC), .PCL_RD(PC_L_RD), .PCH_RD(PC_H_RD), .IR0_RD(IR0_RD),
    .IR1_RD(IR1_RD), .IR2_RD(IR2_RD), .SP_INC(SP_INC), .SP_DEC(SP_DEC), .REG_RD(REG_RD),
    .DB_WR_DEV(DB_WR_DEV), .AB_WR_DEV(microcode_1_ab_wr_dev));  // open: uPC_CLR
  or or_1 (or_1_out, SP_DEC, SP_INC);
  // Probe on microcode_1_ab_wr_dev
  _16_bit_presettable_counter PC (
    .en(PC_INC), .c(clk), .dir(1'b0), .lo_in(instruction_decoder_1_p1), .lo_ld(PC_L_RD),
    .hi_in(instruction_decoder_1_p1), .hi_ld(PC_H_RD), .clr(1'b0), .ovf(PC_ovf), .lo(PC_lo), .hi(PC_hi));
  _16_bit_presettable_counter PC_2 (
    .en(or_1_out), .c(clk), .dir(SP_DEC), .lo_in(instruction_decoder_1_p1), .lo_ld(SP_L_RD),
    .hi_in(instruction_decoder_1_p1), .hi_ld(SP_H_RD), .clr(1'b0), .ovf(PC_2_ovf), .lo(PC_2_lo), .hi(PC_2_hi));
  LED led_1 (.in(PC_ovf));
  assign driver_1_out = 1'b0 ? {PC_hi, PC_lo} : 16'bz;  // Driver driver_1
  LED led_2 (.in(PC_2_ovf));
  assign driver_1_out = 1'b0 ? {PC_2_hi, PC_2_lo} : 16'bz;  // Driver driver_2
  assign driver_3_out = SP_L_WR_DB ? PC_2_lo : 8'bz;  // Driver driver_3
  assign driver_3_out = SP_H_WR_DB ? PC_2_hi : 8'bz;  // Driver driver_4
  assign driver_1_out = 1'b0 ? driver_8_out : 16'bz;  // Driver driver_5
  Register #(.Bits(8)) IR0 (.D(instruction_decoder_1_p1), .C(clk), .en(IR0_RD), .Q(IR0_D));
  Register #(.Bits(8)) A (.D(instruction_decoder_1_p1), .C(clk), .en(REG_A_RD), .Q(A_q));
  Register #(.Bits(8)) B (.D(instruction_decoder_1_p1), .C(clk), .en(REG_B_RD), .Q(B_q));
  Register #(.Bits(8)) C (.D(instruction_decoder_1_p1), .C(clk), .en(REG_C_RD), .Q(C_q));
  Register #(.Bits(8)) D (.D(instruction_decoder_1_p1), .C(clk), .en(REG_D_RD), .Q(D_q));
  // instruction_decoder instruction_decoder_1: pin names not known; wires that end beside it: instruction_decoder_1_p1, driver_1_out, ll, IR0_D, ooo, instruction_decoder_1_p6, vvv, instruction_decoder_1_p8, imm8, rs0, rs1, imm16
  Register #(.Bits(8)) IR1 (.D(instruction_decoder_1_p1), .C(clk), .en(IR1_RD), .Q(instruction_decoder_1_p6));
  assign instruction_decoder_1_p1 = A_WR_DB ? A_q : 8'bz;  // Driver driver_6
  assign driver_8_out[7:0] = ADDR_RS1_A ? A_q : 8'bz;  // Driver driver_7
  assign driver_8_out[15:8] = ADDR_RS0_A ? A_q : 8'bz;  // Driver driver_8
  assign instruction_decoder_1_p1 = B_WR_DB ? B_q : 8'bz;  // Driver driver_9
  assign driver_8_out[7:0] = ADDR_RS1_B ? B_q : 8'bz;  // Driver driver_10
  assign driver_8_out[15:8] = ADDR_RS0_B ? B_q : 8'bz;  // Driver driver_11
  assign instruction_decoder_1_p1 = C_WR_DB ? C_q : 8'bz;  // Driver driver_12
  assign driver_8_out[7:0] = ADDR_RS1_C ? C_q : 8'bz;  // Driver driver_13
  assign driver_8_out[15:8] = ADDR_RS0_C ? C_q : 8'bz;  // Driver driver_14
  assign instruction_decoder_1_p1 = D_WR_DB ? D_q : 8'bz;  // Driver driver_15
  assign driver_8_out[7:0] = ADDR_RS1_D ? D_q : 8'bz;  // Driver driver_16
  assign driver_8_out[15:8] = ADDR_RS0_D ? D_q : 8'bz;  // Driver driver_17
  Register #(.Bits(8)) IR2 (.D(instruction_decoder_1_p1), .C(clk), .en(IR2_RD), .Q(instruction_decoder_1_p8));
  assign driver_3_out = ALU_A_IN_B ? A_q : 8'bz;  // Driver driver_18
  assign driver_19_out = ALU_A_IN_A ? A_q : 8'bz;  // Driver driver_19
  assign driver_3_out = ALU_B_IN_B ? B_q : 8'bz;  // Driver driver_20
  assign driver_19_out = ALU_B_IN_A ? B_q : 8'bz;  // Driver driver_21
  assign driver_3_out = ALU_C_IN_B ? C_q : 8'bz;  // Driver driver_22
  assign driver_19_out = ALU_C_IN_A ? C_q : 8'bz;  // Driver driver_23
  assign driver_3_out = ALU_D_IN_B ? D_q : 8'bz;  // Driver driver_24
  assign driver_19_out = ALU_D_IN_A ? D_q : 8'bz;  // Driver driver_25
  assign driver_3_out = 1'b0 ? imm8 : 8'bz;  // Driver driver_26
  // alu alu_1: pin names not known; wires that end beside it: ooo, driver_3_out, driver_19_out, alu_1_p4, alu_1_p5, alu_1_p6
  nand nand_1 (nand_1_out, ll[0], ll[1]);
  assign driver_19_out = nand_1_out ? ACC_q : 8'bz;  // Driver driver_27
  assign instruction_decoder_1_p1 = 1'b0 ? ACC_q : 8'bz;  // Driver driver_28
  Register #(.Bits(4)) Flag (.D(alu_1_p6), .C(clk), .en(1'b0), .Q(alu_1_p5));
  Decoder #(.Selector_Bits(2)) decoder_1 (
    .sel(vvv[1:0]), .out_0(ALU_A_IN_B), .out_1(ALU_B_IN_B), .out_2(ALU_C_IN_B), .out_3(ALU_D_IN_B));
  Decoder #(.Selector_Bits(2)) decoder_2 (
    .sel(rs0[1:0]), .out_0(ALU_A_IN_A), .out_1(ALU_B_IN_A), .out_2(ALU_C_IN_A), .out_3(ALU_D_IN_A));
  Register #(.Bits(8)) ACC (.D(alu_1_p4), .C(clk), .en(1'b0), .Q(ACC_q));
  Decoder #(.Selector_Bits(3)) decoder_3 (
    .sel(DB_WR_DEV), .out_0(A_WR_DB), .out_1(B_WR_DB), .out_2(C_WR_DB), .out_3(D_WR_DB), .out_6(SP_L_WR_DB),
    .out_7(SP_H_WR_DB));  // open: out_4, out_5
  Decoder #(.Selector_Bits(2)) decoder_4 (
    .sel(rs0[1:0]), .out_0(ADDR_RS0_A), .out_1(ADDR_RS0_B), .out_2(ADDR_RS0_C), .out_3(ADDR_RS0_D));
  Decoder #(.Selector_Bits(2)) decoder_5 (
    .sel(rs1[1:0]), .out_0(ADDR_RS1_A), .out_1(ADDR_RS1_B), .out_2(ADDR_RS1_C), .out_3(ADDR_RS1_D));
  Decoder #(.Selector_Bits(3)) decoder_6 (
    .sel(REG_RD), .out_0(REG_A_RD), .out_1(REG_B_RD), .out_2(REG_C_RD), .out_3(REG_D_RD), .out_6(SP_L_RD),
    .out_7(SP_H_RD));  // open: out_4, out_5

  // Notes on the sheet:
  //   Stack Pointer
  //   Program Counter
  //   DBUS
  //   ABUS
  //   Instruction Register
  //   Registers
  //   Decoder
  //   ALU
  //   ALU BUS
  //   ALU Decoders
  //   ACC
  //   Flag register
  //   Address Decoders
endmodule
